# Fritzing sketch MS_Circuit Schematic (saved by Fritzing 0.9.7b)

parts:
  Part1 = Black Joystick KY-023
  OLED1 = OLED 128x64 I2C Monochrome Display
  Part2 = Arduino Pro Micro (Clone)
  BUTTON2 = Arcade Button (white)
  BUTTON3 = Arcade Button (white)
  BUTTON4 = Arcade Button (white)
  BUTTON5 = Arcade Button (white)
  LED1 = LED - 5mm [color="Blue (430nm)" current=0.030 package="5 mm [THT]"]
  LED2 = LED - 5mm [color="Blue (430nm)" current=0.030 package="5 mm [THT]"]
  R2 = Resistor [tolerance=±5% power=0.25 resistance=220 package=THT]
  R4 = Resistor [tolerance=±5% power=0.25 resistance=220 package=THT]
  LED5 = LED - 5mm [color="Blue (430nm)" current=0.030 package="5 mm [THT]"]
  R5 = Resistor [tolerance=±5% power=0.25 resistance=220 package=THT]
  LED6 = LED - 5mm [color="Blue (430nm)" current=0.030 package="5 mm [THT]"]
  R6 = Resistor [tolerance=±5% power=0.25 resistance=220 package=THT]

nets:
  N1: Part1.SW, Part2.A1
  N2: Part1.VRy, Part2.A2
  N3: Part1.VRx, Part2.A3
  N4: OLED1.SCK, Part2.D3
  N5: OLED1.SDA, Part2.D2
  N6: Part2.GND, LED1.cathode, LED2.cathode, LED5.cathode, LED6.cathode
  N7: Part2.D6, R6.Pin_1
  N8: Part2.D7, R5.Pin_1
  N9: Part2.D8, R2.Pin_1
  N10: Part2.D9, R4.Pin_1
  N11: Part2.D10, BUTTON4.no_name_yet#2
  N12: Part2.D16, BUTTON3.no_name_yet#2
  N13: Part2.D14, BUTTON5.no_name_yet#2
  N14: Part2.D15, BUTTON2.no_name_yet#2
  N15: BUTTON2.no_name_yet#1, BUTTON3.no_name_yet#1, BUTTON4.no_name_yet#1, BUTTON5.no_name_yet#1
  N16: LED1.anode, R2.Pin_0
  N17: LED2.anode, R4.Pin_0
  N18: LED5.anode, R5.Pin_0
  N19: LED6.anode, R6.Pin_0

notes:
  Button 0
  Button 1
  Button 2
  Button 3
  Led 1
  Led 2
  Led 3
  Joystick KY-023
  Oled Display I2C
  Arduino Pro Micro
  Led 0

custom parts:
  Black Joystick KY-023: Description: The joystick is a combination of 2 analoog potentiometer and a digital switch. Arduino GND --> Module pin - Arduino +5V --> Module pin +5V Arduino Analoog 0 --> Module VRx Arduino Analoog 1 --> Module VRy Arduino Digital --> Module SW Dimensions: 1" x 1.25"
  Arcade Button (white): Adafruit Arcade Button (white)
